# Fritzing sketch repeater (saved by Fritzing 0.9.3b)
perfboards: 1

parts:
  R1 = Resistor [tolerance=±5% resistance=10k package=THT]
  Q1 = NPN-Transistor [part_number=2n2222a package="TO92 [THT]"]
  D1 = Rectifier Diode [part_number=1N4001 package="300 mil [THT]"]
  S1 = Toggle Switch [package=THT]  # not connected
  Mod1 = STM32F303  # not connected
  U1 = Optocoupler [package=THT]  # not connected

nets:
  N1: R1.Pin_0, Q1.B, D1.cathode
  N2: Q1.C, D1.anode

notes:
  GND
  COS In
  To PTT
  RX COS

custom parts:
  STM32F303: Medium density Cortex-M3 microcontroller.
